# Fritzing sketch Gif_Box_Led (saved by Fritzing 0.9.1b)
breadboards: 1

parts:
  Bauteil1 = Arduino Nano (Rev3.0)
  J1 = double row female pin header, 8 pins [form="♀ (female)"]

nets:
  N1: Bauteil1.GND, J1.pin1
  N2: Bauteil1.D10, J1.pin4
  N3: Bauteil1.D11/MOSI, J1.pin5
  N4: Bauteil1.D12/MISO, J1.pin7
  N5: Bauteil1.3V3, J1.pin2
  N6: Bauteil1.D13/SCK, J1.pin6
